# Fritzing sketch MiniReed_Esp32 (saved by Fritzing 0.9.6b)

parts:
  U1 = ESP32-38PinWide [part_number=ESP32-38PinWide]
  Mod1 = KY-021 Mini Magnetic Reed Switch Module [package="Breakout board"]

nets (from the breadboard view):
  N1: U1.3.3, Mod1.Vin
  N2: U1.GND, Mod1.-
  N3: U1.GPIO4, Mod1.S

custom parts:
  ESP32-38PinWide: Generic 38-Pin ESP32 with wide format (only access to one side of pins on a breadboard) based on Stephen Lilley's HiLetgo ESP-WROOM-32 ESP32 ESP-32S Development Board.
  KY-021 Mini Magnetic Reed Switch Module: KY-021 magnetic reed switch module. A reed switch is a magnetic sensor that is normally open and gets closed when exposed to a magnetic field.

// code stored in the sketch: Untitled.ino
int led = 2; // LED pin
int reelSwitch = 4; // magnetic senso rpin
int switchState; // variable to store reel switch value
void setup() 
{
  pinMode (led, OUTPUT);
  pinMode (reelSwitch, INPUT);
}
void loop()
{
  switchState = digitalRead(reelSwitch); // read the value of digital interface 2 and assign it to switchState
  
  if (switchState == HIGH) // when the magnetic sensor detect a signal, LED is flashing
  {
    digitalWrite(led, HIGH);
  }
  else 
  {
    digitalWrite(led, LOW);
  }
}
