# Fritzing sketch Botton_Esp32 (saved by Fritzing 0.9.6b)

parts:
  S1 = Pushbutton [package="[THT]"]
  U1 = ESP32-38PinWide [part_number=ESP32-38PinWide]

nets:
  N1: S1.Pin_1, S1.Pin_2, U1.3.3
  N2: S1.Pin_3, S1.Pin_4, U1.GND, U1.GPIO4

custom parts:
  ESP32-38PinWide: Generic 38-Pin ESP32 with wide format (only access to one side of pins on a breadboard) based on Stephen Lilley's HiLetgo ESP-WROOM-32 ESP32 ESP-32S Development Board.

// code stored in the sketch: Untitled.ino
#define boton 4
int contador = 0;

void setup(){
pinMode(boton, INPUT);
Serial.begin(9600);
}

void loop(){
  int estado = digitalRead(boton);
  if (estado == HIGH){
    contador++;
    Serial.println(contador);
    delay(1000);
  }
}
