# Fritzing sketch HeartBeat_Esp32 (saved by Fritzing 0.9.6b)

parts:
  U1 = ESP32-38PinWide [part_number=ESP32-38PinWide]
  SEN1 = Pulse Sensor [package=SIP]

nets (from the breadboard view):
  N1: U1.3.3, SEN1.Vcc
  GND: U1.GND, SEN1.GND
  N2: U1.GPIO4, SEN1.Signal

custom parts:
  ESP32-38PinWide: Generic 38-Pin ESP32 with wide format (only access to one side of pins on a breadboard) based on Stephen Lilley's HiLetgo ESP-WROOM-32 ESP32 ESP-32S Development Board.
  Pulse Sensor: Pulse Sensor Optical Heart Rate Monitor for Arduino and other microcontrollers

// code stored in the sketch: Untitled.ino
int PulseSensorPurplePin = 4;        // Pulse Sensor PURPLE WIRE connected to ANALOG PIN 0
int LED13 = 2;   //  The on-board Arduion LED


int Signal;                // holds the incoming raw data. Signal value can range from 0-1024
int Threshold = 550;            // Determine which Signal to "count as a beat", and which to ingore.


// The SetUp Function:
void setup() {
  pinMode(LED13,OUTPUT);         // pin that will blink to your heartbeat!
   Serial.begin(9600);         // Set's up Serial Communication at certain speed.

}

// The Main Loop Function
void loop() {

  Signal = analogRead(PulseSensorPurplePin);  // Read the PulseSensor's value.
                                              // Assign this value to the "Signal" variable.

   Serial.println(Signal);                    // Send the Signal value to Serial Plotter.


   if(Signal > Threshold){                          // If the signal is above "550", then "turn-on" Arduino's on-Board LED.
     digitalWrite(LED13,HIGH);
   } else {
     digitalWrite(LED13,LOW);                //  Else, the sigal must be below "550", so "turn-off" this LED.
   }


delay(10);


}
