# Fritzing sketch TwoColor_Esp32 (saved by Fritzing 0.9.6b)

parts:
  U1 = ESP32-38PinWide [part_number=ESP32-38PinWide]
  Mod1 = KY-011 Two Color LED Module [package="Breakout board"]

nets (from the breadboard view):
  N1: U1.GND, Mod1.S
  N2: U1.GPIO2, Mod1.-
  N3: U1.GPIO4, Mod1.Vin

custom parts:
  ESP32-38PinWide: Generic 38-Pin ESP32 with wide format (only access to one side of pins on a breadboard) based on Stephen Lilley's HiLetgo ESP-WROOM-32 ESP32 ESP-32S Development Board.
  KY-011 Two Color LED Module: KY-011 Two Color LED Module consist of a common cathode 3mm red/green LED.

// code stored in the sketch: Untitled.ino
int redpin = 4; // pin for red signal
int greenpin = 2; // pin for green signal
int val;
void setup() {
	pinMode(redpin, OUTPUT);
	pinMode(greenpin, OUTPUT);
}
void loop() {
	for(val = 255; val > 0; val--) { 
		analogWrite(redpin, val); //dim red
		analogWrite(greenpin, 255 - val); // brighten green
		delay(15);
	}
	for(val = 0; val < 255; val++) { 
		analogWrite(redpin, val); //brighten red
		analogWrite(greenpin, 255 - val); //dim green
		delay(15);
	}
}
