# Fritzing sketch MotorDCBallSwitch_Esp32 (saved by Fritzing 0.9.6b)

parts:
  U1 = ESP32-38PinWide [part_number=ESP32-38PinWide]
  Mod1 = KY-020 Tilt Switch Module [package="Breakout board"]
  L298N1 = L298N DC motor driver
  M1 = DC Motor

nets (from the breadboard view):
  N1: U1.3.3, Mod1.Vin
  GND: U1.GND, Mod1.-, L298N1.GND
  VIN: U1.VIN, L298N1.12V
  N2: U1.GPIO2, L298N1.IN3
  N3: U1.GPIO4, Mod1.S
  N4: U1.GPIO5, L298N1.IN4
  N5: L298N1.OUT3, M1.pin_2
  N6: L298N1.OUT4, M1.pin_1

custom parts:
  ESP32-38PinWide: Generic 38-Pin ESP32 with wide format (only access to one side of pins on a breadboard) based on Stephen Lilley's HiLetgo ESP-WROOM-32 ESP32 ESP-32S Development Board.
  KY-020 Tilt Switch Module: KY-020 tilt switch sensor module. Closes the circuit when it is tilted to the side as long as it is moved with enough force and degree of inclination to activate the ball switch inside.
  L298N DC motor driver: 2x DC motor driver with 78M05 positive voltage regulator (7..35 V) L298N: max 46 V, 2 A Set 5 V Enable jumper to enable 5 V regultor (needed for the L298N) and +5 V output at screw terminal or supply external +5 V at screw terminal Set ENA and/or ENB to +5 V to enable motor permanently or supply ENA and/or ENB with PWM signal IN1 and IN2 set rotation directory for motor A (OUT1/OUT2) IN2 and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

// code stored in the sketch: Untitled.ino
#include <TM1637Display.h>

#define boton 4
int contador = 0;
const int CLK = 2;
const int DIO = 5;

TM1637Display display(CLK, DIO);

const uint8_t linea[] = {
  SEG_G, SEG_G, SEG_G, SEG_G
};

void setup(){
pinMode(boton, INPUT);
Serial.begin(115200);
display.setBrightness(5);
}

void loop(){
int estado = digitalRead(boton);
if (estado == HIGH){
  contador++;
Serial.println(contador);
display.setSegments(linea);
delay(1000);
}
}
