# Fritzing sketch Shock_Esp32 (saved by Fritzing 0.9.6b)

parts:
  U1 = ESP32-38PinWide [part_number=ESP32-38PinWide]
  SW-1 = Vibration sensor module

nets (from the breadboard view):
  N1: U1.3.3, SW-1.vcc
  N2: U1.GND, SW-1.Ground
  N3: U1.GPIO4, SW-1.Digital_output

custom parts:
  ESP32-38PinWide: Generic 38-Pin ESP32 with wide format (only access to one side of pins on a breadboard) based on Stephen Lilley's HiLetgo ESP-WROOM-32 ESP32 ESP-32S Development Board.
  Vibration sensor module: Single-roller type full induction trigger switch. When no vibration or tilt, the product is ON conduction state, and in the steady state, when a vibration or tilt, the switch will be rendered instantly disconnect the conductive resistance increases, generating a current pulse signal, thereby triggering circuit. The default state of the swith is close Digital output Supply voltage:3.3V-5V On-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

// code stored in the sketch: Untitled.ino
int ledpin=2;                   // Set led pin at Arduino pin 11
int shocksensor=4;               // Set sensor pin at Arduino pin 8
int sensorvalue;                 // initialize variable to store sensor data
void setup()
{
 pinMode(ledpin,OUTPUT);       // LED pin set to output
 pinMode(shocksensor,INPUT);  //shock sensor pin set to input
 Serial.begin(9600);        // set baud rate for Serial communication
}
void loop() 
{
 sensorvalue = digitalRead(shocksensor); // read values from sensor pin and store in variable
 if (sensorvalue==HIGH)      // if shake detected
 // if (sensorvalue==LOW)  // for pull-up configuration
 {
  digitalWrite(ledpin,HIGH);   // turn LED on
  Serial.println("vibration detected system awake"); // Print message 
 }
 else{
  digitalWrite(ledpin,LOW);   // turn LED off
  Serial.println("Sleep mode");  // Print message
 }
 delay(20);                   // delay 
}
