# Fritzing sketch 7colorFlash_Esp32 (saved by Fritzing 0.9.6b)

parts:
  U1 = ESP32-38PinWide [part_number=ESP32-38PinWide]
  Mod1 = KY-034 Automatic Flashing Color LED [package="Breakout board"]

nets:
  N1: U1.GND, U1.GPIO4, Mod1.-
  N2: U1.GPIO13, Mod1.S

custom parts:
  ESP32-38PinWide: Generic 38-Pin ESP32 with wide format (only access to one side of pins on a breadboard) based on Stephen Lilley's HiLetgo ESP-WROOM-32 ESP32 ESP-32S Development Board.
  KY-034 Automatic Flashing Color LED: KY-034 Automatic Flashiing Color LED. A 7 color LED that flashes through a sequence of colors, creating a multicolored pattern of flashing light.

// code stored in the sketch: Untitled.ino
int pin = 13;
void setup() {
  Serial.begin(9600);
  pinMode(pin, OUTPUT);
}
void loop() {
  digitalWrite(pin, HIGH);
  Serial.println("Encendido");
  delay (10000);
  digitalWrite(pin, LOW);
  Serial.println("Apagado");
  delay (1000);
}
