# Fritzing sketch ReedSwitch&Servo_Esp32 (saved by Fritzing 0.9.6b)

parts:
  U1 = ESP32-38PinWide [part_number=ESP32-38PinWide]
  Mod1 = KY-025 Reed Switch Module [package="Breakout board"]
  J1 = Basic Servo  # not connected

nets (from the breadboard view):
  N1: U1.3.3, Mod1.+
  N2: U1.GND, Mod1.G
  N3: U1.GPIO4, Mod1.A0

custom parts:
  ESP32-38PinWide: Generic 38-Pin ESP32 with wide format (only access to one side of pins on a breadboard) based on Stephen Lilley's HiLetgo ESP-WROOM-32 ESP32 ESP-32S Development Board.
  KY-025 Reed Switch Module: KY-025 Reed Switch Module, it reacts in the presence of a magnetic field.

// code stored in the sketch: Untitled.ino
#include <ESP32Servo.h>

const int pinSensor = 4;
const int pinLED = 2;
Servo myServo;

void setup() {
  //configurar pin como entrada con resistencia pull-up interna
  pinMode(pinSensor, INPUT_PULLUP);
  pinMode(pinLED, OUTPUT);
  Serial.begin(115200);
  Serial.println("Example servo");
  //Initializing servo object
  myServo.attach(2);
}

void loop() {
  int value = digitalRead(pinSensor);

  if (value == LOW) {
    digitalWrite(pinLED, HIGH);
    myServo.write(90);
  } else {
    digitalWrite(pinLED, LOW);
    myServo.write(0);
  }

  delay(1000);
}
