# Fritzing sketch AnalogTemp_Esp32 (saved by Fritzing 0.9.6b)

parts:
  U1 = ESP32-38PinWide [part_number=ESP32-38PinWide]
  KY-1 = Keyes Analog Temp Sensor [package=THT]

nets (from the breadboard view):
  N1: U1.3.3, KY-1.power
  N2: U1.GND, KY-1.ground
  N3: U1.GPIO4, KY-1.signal

custom parts:
  ESP32-38PinWide: Generic 38-Pin ESP32 with wide format (only access to one side of pins on a breadboard) based on Stephen Lilley's HiLetgo ESP-WROOM-32 ESP32 ESP-32S Development Board.
  Keyes Analog Temp Sensor: Keyes Analog Temperature Sensor Module for Arduino.

// code stored in the sketch: Untitled.ino
void setup() {
  Serial.begin(9600);   // initialize serial interface with baud 9600bps
}

void loop() {
  // Read value from module connected at pin A0
  int V_input = analogRead(4);

  // calculate thermometer resistance by comparing it to the modules onboard 10K-ohm resistor
  float R_ohms = 10000 * (1023.0 / (float)V_input - 1.0);

  // calculate temperature in Celsius
  float temp_C = (1.0 / (0.001129148 + (0.000234125*log(R_ohms)) + 0.0000000876741*log(R_ohms)*log(R_ohms)*log(R_ohms)))-273.15;

  // output result to serial
  Serial.print("Temperature (degC): ");
  Serial.println(temp_C);
}
