# Fritzing sketch DigitalTemp_Esp32 (saved by Fritzing 0.9.6b)

parts:
  U1 = ESP32-38PinWide [part_number=ESP32-38PinWide]
  Mod1 = KY-028 Digital Temperature Sensor Module [package="Breakout board"]

nets (from the breadboard view):
  N1: U1.3.3, Mod1.+
  N2: U1.GPIO27, Mod1.A0
  N3: U1.GND, Mod1.G
  N4: U1.GPIO4, Mod1.D0

custom parts:
  ESP32-38PinWide: Generic 38-Pin ESP32 with wide format (only access to one side of pins on a breadboard) based on Stephen Lilley's HiLetgo ESP-WROOM-32 ESP32 ESP-32S Development Board.
  KY-028 Digital Temperature Sensor Module: KY-028 Digital Temperature Sensor Module, used to measure changes in temperature.

// code stored in the sketch: Untitled.ino
int led = 2; // define the LED pin
int digitalPin = 2; // KY-028 digital interface
int analogPin = 27; // KY-028 analog interface
int digitalVal; // digital readings
int analogVal; //analog readings
void setup()
{
  pinMode(led, OUTPUT);
  pinMode(digitalPin, INPUT);
  //pinMode(analogPin, OUTPUT);
  Serial.begin(9600);
}
void loop()
{
  // Read the digital interface
  digitalVal = digitalRead(digitalPin); 
  if(digitalVal == HIGH) // if temperature threshold reached
  {
    digitalWrite(led, HIGH); // turn ON Arduino's LED
  }
  else
  {
    digitalWrite(led, LOW); // turn OFF Arduino's LED
  }
  // Read the analog interface
  analogVal = analogRead(analogPin); 
  Serial.println(analogVal); // print analog value to serial
  delay(100);
}
