# Fritzing sketch IrReceptorStepper_Esp32 (saved by Fritzing 0.9.6b)

parts:
  U1 = ESP32-38PinWide [part_number=ESP32-38PinWide]
  Mod1 = KY-022 Infrared Receiver Module [package="Breakout board"]
  M1 = Stepper Motor - Bipolar  # not connected

nets:
  N1: U1.3.3, Mod1.Vin
  N2: U1.GND, U1.GPIO4, Mod1.-
  N3: U1.GPIO15, Mod1.S

custom parts:
  ESP32-38PinWide: Generic 38-Pin ESP32 with wide format (only access to one side of pins on a breadboard) based on Stephen Lilley's HiLetgo ESP-WROOM-32 ESP32 ESP-32S Development Board.
  KY-022 Infrared Receiver Module: KY-022 IR receiver module, reacts to 38kHz infrared light.

// code stored in the sketch: Untitled.ino
#include <Stepper.h>
#include <IRremote.h>

int RECV_PIN = 15;

IRrecv irrecv(RECV_PIN);
 
decode_results results;

int val;
double stepsPerRevolution = 2048;
Stepper myStepper(stepsPerRevolution, 8, 10, 9, 11);  // Pin inversion to make the library work

void setup() {
  irrecv.enableIRIn(); // Start the receiver
  myStepper.setSpeed(10);
  Serial.begin(9600);
}

void loop(){
  val = digitalRead (Shock);
if (irrecv.decode(&results))
{
Serial.println("Detecta infrarojos");
  myStepper.step(stepsPerRevolution);
}else{
  Serial.println("No detecta infrarojos");
  myStepper.step(-stepsPerRevolution);
}  
}
