# Fritzing sketch EncoderLed7Seg_Esp32 (saved by Fritzing 0.9.6b)

parts:
  U1 = ESP32-38PinWide [part_number=ESP32-38PinWide]
  RE1 = Rotary Encoder [package=THT]
  7_Segment1 = 7 Segment Display

nets:
  N1: U1.GPIO12, RE1.EncoderPinB
  N2: U1.GND, U1.GPIO4, RE1.EncoderPinC, 7_Segment1.Segment_D
  N3: U1.GPIO2, RE1.EncoderPinA
  N4: U1.GPIO5, 7_Segment1.Segment_DP

custom parts:
  ESP32-38PinWide: Generic 38-Pin ESP32 with wide format (only access to one side of pins on a breadboard) based on Stephen Lilley's HiLetgo ESP-WROOM-32 ESP32 ESP-32S Development Board.

// code stored in the sketch: Untitled.ino
#include <TM1637Display.h>

#define CLK 4
#define DIO 5
#define encoderPinA 2
#define encoderPinB 12

int encoderPos = 0;
int lastPos = -1;
volatile bool encoderASet = false;
volatile bool encoderBSet = false;

TM1637Display display(CLK, DIO);

void ICACHE_RAM_ATTR encoder() {
  encoderASet = digitalRead(encoderPinA);
  encoderBSet = digitalRead(encoderPinB);
  if (encoderASet != encoderBSet) {
    if (digitalRead(encoderPinB) == HIGH) {
      encoderPos++;
    } else {
      encoderPos--;
    }
  } else {
    if (digitalRead(encoderPinA) == HIGH) {
      encoderPos++;
    } else {
      encoderPos--;
    }
  }
}

void setup() {
  pinMode(encoderPinA, INPUT_PULLUP);
  pinMode(encoderPinB, INPUT_PULLUP);
  attachInterrupt(digitalPinToInterrupt(encoderPinA), encoder, CHANGE);
  attachInterrupt(digitalPinToInterrupt(encoderPinB), encoder, CHANGE);

  display.setBrightness(0x0f);
}

void loop() {
  if (encoderPos != lastPos) {
    display.showNumberDec(encoderPos);
    lastPos = encoderPos;
  }
}
