# Fritzing sketch MatrizLed_Esp32 (saved by Fritzing 0.9.6b)

parts:
  U1 = ESP32-38PinWide [part_number=ESP32-38PinWide]
  S1 = Pushbutton [package="[THT]"]
  RGB_SMD_LED1 = SMD RGB LED (WS2812) [package=5050]

nets (from the breadboard view):
  N1: U1.3.3, S1.Pin_1
  N2: U1.GND, U1.GPIO15, S1.Pin_3, S1.Pin_4
  N3: U1.GPIO11, RGB_SMD_LED1.VSS
  VIN: U1.VIN, RGB_SMD_LED1.VDD
  N4: U1.GPIO2, RGB_SMD_LED1.NC

custom parts:
  ESP32-38PinWide: Generic 38-Pin ESP32 with wide format (only access to one side of pins on a breadboard) based on Stephen Lilley's HiLetgo ESP-WROOM-32 ESP32 ESP-32S Development Board.

// code stored in the sketch: Untitled.ino
#include <Adafruit_GFX.h>
#include <Adafruit_NeoMatrix.h>
#include <Adafruit_NeoPixel.h>
#ifndef PSTR
#define PSTR // Make Arduino Due happy
#endif

#define PIN 6
int btn = 8;
int val;
String res;

// Forma en la que se va a imprimir el valor
Adafruit_NeoMatrix matrix = Adafruit_NeoMatrix(8, 8, 4, 1, PIN,
  NEO_TILE_TOP   + NEO_TILE_LEFT   + NEO_TILE_COLUMNS   + NEO_TILE_PROGRESSIVE +
  NEO_MATRIX_TOP + NEO_MATRIX_LEFT + NEO_MATRIX_COLUMNS + NEO_MATRIX_ZIGZAG,
  NEO_GRB + NEO_KHZ800);

const uint16_t colors[] = {
  matrix.Color(255, 0, 0), matrix.Color(0, 255, 0), matrix.Color(0, 0, 255) };

void setup() {
  matrix.begin();
  matrix.setTextWrap(false);
  matrix.setBrightness(40);
  matrix.setTextColor(colors[0]);
  pinMode (btn, INPUT);
  Serial.begin(9600);
}

int x    = matrix.width();
int pass = 0;

void loop() {
  // Se lee el sensor y de acuerdo al valor se muestra un mensaje en la matríz
  val = digitalRead (btn);
  if (val == HIGH) {
    res = "Sin presionar";
  }else{
    res = "Presionado";
  }
  String imp = "Erik Daniel Méndez"+res;
  Serial.println(imp);
  
  // Mover el mensaje por la matríz
  matrix.fillScreen(0);
  matrix.setCursor(x, 0);
  matrix.print(imp);
  if(--x < -150) {
    x = matrix.width();
    if(++pass >= 3) pass = 0;
    matrix.setTextColor(colors[pass]);
  }
  matrix.show();
  delay(100);
}
